# Fritzing sketch Montagem (saved by Fritzing 0.9.3b)
breadboards: 1

parts:
  Componente1 = Arduino Uno (Rev3)
  J1 = Piezo Speaker
  Componente2 = HC-SR501 Body Sensor Module

nets:
  N1: Componente1.D8, J1.pin2
  N2: Componente1.D3_PWM, Componente2.OUT
  5V: Componente1.5V, Componente2.VCC
  GND: Componente1.GND, J1.pin1, Componente2.GND

custom parts:
  HC-SR501 Body Sensor Module: Pyroelectric Infrared PIR Motion Sensor Detector Module
